// Logisim project 2_s Compliment.circ as structural Verilog: 1 circuit, main circuit main
module main (
  input  A,
  input  B,
  input  C,
  input  D,
  output S0,
  output S1,
  output S2,
  output S3
);

  wire and_1_out, and_2_out, and_3_out, and_4_out, and_5_out, and_6_out, and_7_out, and_8_out, and_9_out,
       not_1_out, not_2_out, not_3_out, not_4_out, not_5_out, not_6_out, not_7_out, not_8_out, not_9_out,
       not_10_out;

  not not_1 (not_1_out, A);
  not not_2 (not_2_out, D);
  not not_3 (not_3_out, C);
  not not_4 (not_4_out, B);
  not not_5 (not_5_out, B);
  not not_6 (not_6_out, B);
  not not_7 (not_7_out, C);
  and and_1 (and_1_out, not_1_out, C);
  and and_2 (and_2_out, not_1_out, D);
  and and_3 (and_3_out, not_1_out, not_2_out, B);
  and and_4 (and_4_out, A, not_2_out, not_3_out, not_4_out);
  and and_5 (and_5_out, not_5_out, D);
  and and_6 (and_6_out, not_6_out, C);
  not not_8 (not_8_out, C);
  not not_9 (not_9_out, D);
  and and_7 (and_7_out, not_7_out, D);
  not not_10 (not_10_out, D);
  and and_8 (and_8_out, B, not_8_out, not_9_out);
  and and_9 (and_9_out, C, not_10_out);
  or or_1 (S0, and_1_out, and_2_out, and_3_out, and_4_out);
  or or_2 (S1, and_5_out, and_6_out, and_8_out);
  or or_3 (S2, and_7_out, and_9_out);

  assign S3 = D;

  // Notes on the sheet:
  //   2'S COMPLIMENT OF 4-BIT INPUT
  //   (A'C + A'D +A'BD' +AB'C'D')
  //   (B'D + B'C + BC'D')
  //   (C'D + CD')
  //   (D)
endmodule
