// Logisim project BCD 4 BIT ADDER.circ as structural Verilog: 1 circuit, main circuit main
module main (
  input  [3:0] in_1,
  input  in_2,
  input  in_3,
  input  [3:0] in_4,
  output out_5,
  output out_6,
  output out_7,
  output out_8,
  output out_9
);

  wire adder_1_cout, and_1_out, and_2_out;
  wire [3:0] adder_1_out;

  Adder #(.width(4)) adder_1 (.a(in_1), .b(in_4), .out(adder_1_out), .cout(adder_1_cout));  // open: cin
  and and_1 (and_1_out, adder_1_out[2], adder_1_out[3]);
  and and_2 (and_2_out, adder_1_out[1], adder_1_out[3]);
  or or_1 (out_9, and_2_out, and_1_out, adder_1_cout);
  Adder #(.width(4)) adder_2 (
    .a(adder_1_out), .b({in_2, {2{out_9}}, in_3}), .out({out_5, out_6, out_7, out_8}));  // open: cin, cout

  // Notes on the sheet:
  //   Input-1
  //   Input-2
  //   4-BIT ADDER
  //   Carry
  //   S3.S2
  //   S3.S1
  //   BCD 4-BIT ADDER:
  //   S0
  //   4-BIT ADDER
  //   S4'
  //   S2'
  //   S3'
  //   S0'
  //   S1'
endmodule
