// Logisim project EXCESS-3 ADDER.circ as structural Verilog: 1 circuit, main circuit main
module main (
  input  [3:0] in_1,
  input  in_2,
  input  [3:0] in_3,
  input  _1,
  output out_5,
  output out_6,
  output out_7,
  output out_8,
  output out_9,
  output out_10,
  output out_11,
  output out_12
);

  wire [3:0] adder_1_out;
  wire [3:3] not_1_out;

  Adder #(.width(4)) adder_1 (.a(in_1), .b(in_3), .out(adder_1_out), .cout(out_6));  // open: cin
  not not_1 (not_1_out[3], out_6);
  Adder #(.width(4)) adder_2 (
    .a(adder_1_out), .b({{2{not_1_out[3]}}, out_6, _1}), .out({out_9, out_10, out_11, out_12}));  // open: cin, cout

  assign out_5 = in_2;
  assign out_7 = in_2;
  assign out_8 = in_2;

  // Notes on the sheet:
  //   Excess-3 (input 1)
  //   Excess-3 (input 2)
  //   Carry
  //   S0
  //   S1
  //   S2
  //   S3
  //   EXCESS-3 4-BIT ADDER:
  //   Here when carry is '0' we have to add 3 for the final sum
  //   Here when carry is '1' we have to add 4 bits in front to get the final answer
  //   Here when carry is '1' we have to add 2's compliment of 3 for the final sum
  //   4-BIT ADDER
  //   S7'
  //   S6'
  //   S5'
  //   S4'
  //   S3'
  //   S2'
  //   S0'
  //   S1'
endmodule
