// Logisim project FLIP FLOPS.circ as structural Verilog: 1 circuit, main circuit main
module main (
  input  R,
  input  S,
  input  S_2,
  input  R_2,
  output Q,
  output Q_2,
  output Q_prime,
  output Q_prime_2
);

  nor nor_1 (Q, R, Q_prime);
  nor nor_2 (Q_prime, Q, S_2);
  nand nand_1 (Q_2, S, Q_prime_2);
  nand nand_2 (Q_prime_2, Q_2, R_2);

  // Notes on the sheet:
  //   By NOR Gate
  //   S-R LATCH
  //   By NAND Gate
endmodule
