// Logisim project LAB (6)- 4 BIT DECREAMENTER.circ as structural Verilog: 1 circuit, main circuit main
module main (
  input  _1,
  input  A,
  input  B,
  input  C,
  input  D,
  output S5,
  output S4,
  output S3,
  output S2,
  output S1
);

  wire and_1_out, and_3_out, and_4_out, not_1_out, not_2_out, not_3_out, not_4_out;

  xor xor_1 (S5, _1, A);
  not not_1 (not_1_out, A);
  and and_1 (and_1_out, _1, not_1_out);
  xor xor_2 (S2, and_4_out, D);
  not not_2 (not_2_out, D);
  xor xor_3 (S4, and_1_out, B);
  not not_3 (not_3_out, B);
  xor xor_4 (S3, and_3_out, C);
  not not_4 (not_4_out, C);
  and and_2 (S1, and_4_out, not_2_out);
  and and_3 (and_3_out, and_1_out, not_3_out);
  and and_4 (and_4_out, and_3_out, not_4_out);

  // Notes on the sheet:
  //   ( 1 XOR A)
  //   (1.A')
  //   (A'.B' XOR C)
  //   (A'.B'.C' XOR D)
  //   4 BIT DECREAMENTER
  //   (A' XOR B)
  //   (B'.A')
  //   (A'.B'.C'.D')
  //   (A'.B'.C')
endmodule
