// Logisim project LAB (6)- 4 BIT INCREAMENTER.circ as structural Verilog: 1 circuit, main circuit main
module main (
  input  _1,
  input  A,
  input  B,
  input  C,
  input  D,
  output S5,
  output S4,
  output S3,
  output S2,
  output S1
);

  wire and_1_out, and_2_out, and_3_out;

  xor xor_1 (S5, _1, A);
  and and_1 (and_1_out, _1, A);
  xor xor_2 (S3, and_3_out, C);
  xor xor_3 (S4, and_1_out, B);
  and and_2 (and_2_out, and_3_out, C);
  xor xor_4 (S2, and_2_out, D);
  and and_3 (and_3_out, and_1_out, B);
  and and_4 (S1, and_2_out, D);

  // Notes on the sheet:
  //   (1 X0R A)
  //   (A.1)
  //   4 BIT INCREAMENTER
  //   (A XOR B)
  //   (A.B XOR C)
  //   (A.B)
  //   (A.B.C)
  //   (A.B.C XOR D)
  //   (A.B.C.D)
endmodule
