// Logisim project MULTIPLEXER.circ as structural Verilog: 1 circuit, main circuit main
module main (
  input  Z,
  input  in_2,
  input  in_3,
  input  [1:0] X_Y,
  input  D,
  input  in_6,
  input  in_7,
  input  [2:0] A_B_C,
  input  Z_2,
  input  in_10,
  input  in_11,
  input  [2:0] W_X_Y,
  input  C,
  input  [1:0] A_B,
  input  B,
  input  in_16,
  input  in_17,
  input  [1:0] Cin__A,
  input  in_19,
  input  in_20,
  input  D_2,
  input  [2:0] A_B_C_2,
  output F,
  output F_2,
  output F1,
  output F3,
  output F4,
  output F2
);

  wire not_1_out, not_2_out, not_3_out, not_4_out, not_5_out;

  not not_1 (not_1_out, Z);
  Multiplexer #(.select(2), .enable("false")) multiplexer_1 (
    .in0(Z), .in1(not_1_out), .in2(in_2), .in3(in_3), .out(F), .sel(X_Y));
  not not_2 (not_2_out, D);
  not not_3 (not_3_out, Z_2);
  Multiplexer #(.select(2), .enable("false")) multiplexer_2 (
    .in0(C), .in1(not_4_out), .in2(not_4_out), .in3(C), .out(F3), .sel(A_B));
  not not_4 (not_4_out, C);
  Multiplexer #(.select(2), .enable("false")) multiplexer_3 (
    .in0(B), .in1(in_16), .in2(in_17), .in3(B), .out(F4), .sel(Cin__A));
  not not_5 (not_5_out, D_2);
  Multiplexer #(.select(3), .enable("false")) multiplexer_4 (
    .in0(D), .in1(D), .in2(not_2_out), .in3(in_6), .in4(in_6), .in5(D), .in6(in_7), .in7(in_7), .out(F_2),
    .sel(A_B_C));
  Multiplexer #(.select(3), .enable("false")) multiplexer_5 (
    .in0(Z_2), .in1(in_10), .in2(not_3_out), .in3(not_3_out), .in4(in_11), .in5(not_3_out), .in6(in_11),
    .in7(in_10), .out(F1), .sel(W_X_Y));
  Multiplexer #(.select(3), .enable("false")) multiplexer_6 (
    .in0(in_19), .in1(in_19), .in2(in_20), .in3(not_5_out), .in4(D_2), .in5(D_2), .in6(in_20), .in7(in_20),
    .out(F2), .sel(A_B_C_2));

  // Notes on the sheet:
  //   MULTIPLEXERS:
  //   SUM FUNCTION OF FULL ADDER:
  //   BORROW FUNCTION OF FULL SUBTRACTOR:
  //   F(X,Y,Z)= SUM(1,2,6,7)
  //   F(A,B,C,D)=SUM(1,3,4,11,12,13,14,15)
  //   F2=A'B'C' +A'CD' +AB'C'D +B'CD
  //   F1=X'Y'Z +W'XYZ' +WX'Z' +WY'Z +XY'Z'
endmodule
