// Logisim project Modulo Using T flip-flop.circ as structural Verilog: 1 circuit, main circuit main
module main (
  input  _1,
  output out_2,
  output out_3,
  output out_4,
  output out_5
);

  wire CLK_out, t_ff_1_qn, t_ff_2_qn, t_ff_3_qn;

  Clock CLK (.out(CLK_out));
  T_Flip_Flop t_ff_1 (.clk(CLK_out), .T(_1), .Q(out_5), .Qn(t_ff_1_qn));  // open: preset, reset, en
  T_Flip_Flop t_ff_2 (.clk(t_ff_1_qn), .T(_1), .Q(out_4), .Qn(t_ff_2_qn));  // open: preset, reset, en
  T_Flip_Flop t_ff_3 (.clk(t_ff_2_qn), .T(_1), .Q(out_3), .Qn(t_ff_3_qn));  // open: preset, reset, en
  T_Flip_Flop t_ff_4 (.clk(t_ff_3_qn), .T(_1), .Q(out_2));  // open: Qn, preset, reset, en

  // Notes on the sheet:
  //   AIM:
  //   Concepts Related:
  //   using T flip-flops.
  //   to obtain 3 bit output.
  //   3. Here 4 bit output is generated.
  //   PRACTICAL: 9
  //   1. Here as the name suggest T- FlipFlop, it toggles the input.
  //   4. As the circuit is modifiable, we can remove the 4th Flip-Flop 
  //   Design and implementation of modulo-N Ripple counter 
  //   2. While the input at T end must be fixed as 1, as it works on that state.
endmodule
