// Logisim project REGISTER.circ as structural Verilog: 1 circuit, main circuit main
module main (
  input  SHIFT_RIGHT,
  input  I0,
  input  I1,
  input  [1:0] SELECTION_PIN,
  input  I2,
  input  SHIFT_LEFT,
  input  I3,
  input  CLEAR,
  output A0,
  output A1,
  output A2,
  output A3
);

  wire CLOCK_out, multiplexer_1_out, multiplexer_2_out, multiplexer_3_out, multiplexer_4_out;

  Multiplexer #(.select(2)) multiplexer_1 (
    .in0(A0), .in1(SHIFT_RIGHT), .in2(A1), .in3(I0), .out(multiplexer_1_out), .sel(SELECTION_PIN));  // open: en
  Multiplexer #(.select(2)) multiplexer_2 (
    .in0(A1), .in1(A0), .in2(A2), .in3(I1), .out(multiplexer_2_out), .sel(SELECTION_PIN));  // open: en
  Multiplexer #(.select(2)) multiplexer_3 (
    .in0(A2), .in1(A1), .in2(A3), .in3(I2), .out(multiplexer_3_out), .sel(SELECTION_PIN));  // open: en
  Multiplexer #(.select(2)) multiplexer_4 (
    .in0(A3), .in1(A2), .in2(SHIFT_LEFT), .in3(I3), .out(multiplexer_4_out), .sel(SELECTION_PIN));  // open: en
  Clock CLOCK (.out(CLOCK_out));
  D_Flip_Flop d_ff_1 (.clk(CLOCK_out), .D(multiplexer_1_out), .Q(A0), .reset(CLEAR));  // open: Qn, preset, en
  D_Flip_Flop d_ff_2 (.clk(CLOCK_out), .D(multiplexer_2_out), .Q(A1), .reset(CLEAR));  // open: Qn, preset, en
  D_Flip_Flop d_ff_3 (.clk(CLOCK_out), .D(multiplexer_3_out), .Q(A2), .reset(CLEAR));  // open: Qn, preset, en
  D_Flip_Flop d_ff_4 (.clk(CLOCK_out), .D(multiplexer_4_out), .Q(A3), .reset(CLEAR));  // open: Qn, preset, en

  // Notes on the sheet:
  //   00 -> No Change
  //   Selection Pin States:
  //   01 -> Right Shift Simulates
  //   10 -> Left Shift Simulates
  //   11 -> Parallel Condition
  //   AIM:
  //   CLEAR: It clears all the Current Present Bits.
  //   I0, I1, I2 and I3 works only When Selection Pin is in parallel mode.
  //   PRACTICAL: 10
  //   shift register with parallel load.
  //   Design and implementation of a bidirectional
endmodule
