// Logisim project lAB 6- 3 BIT MULTIPLIER.circ as structural Verilog: 1 circuit, main circuit main
module main (
  input  A,
  input  B,
  input  C,
  input  D,
  input  E,
  input  F
);

  // AND_Gate and_1 is placed but not wired
  // AND_Gate and_2 is placed but not wired
  // AND_Gate and_3 is placed but not wired
  // AND_Gate and_4 is placed but not wired
  // AND_Gate and_5 is placed but not wired
  // AND_Gate and_6 is placed but not wired
endmodule
