// Logisim project lab -7(Multiplier).circ as structural Verilog: 1 circuit, main circuit main
module main (
  input  A2,
  input  A1,
  input  A0,
  input  B2,
  input  B1,
  input  B0,
  output Z5,
  output Z4,
  output Z3,
  output Z2,
  output Z1,
  output Z0
);

  wire adder_1_cout, adder_2_cout, adder_2_out, adder_3_cout, adder_3_out, adder_4_cout, adder_6_cout,
       and_1_out, and_2_out, and_3_out, and_4_out, and_5_out, and_6_out, and_7_out, and_8_out;

  and and_1 (and_1_out, A2, B2);
  and and_2 (and_2_out, A1, B2);
  and and_3 (and_3_out, A0, B2);
  and and_4 (and_4_out, A2, B1);
  and and_5 (and_5_out, A1, B1);
  and and_6 (and_6_out, A0, B1);
  and and_7 (and_7_out, A2, B0);
  and and_8 (and_8_out, A1, B0);
  and and_9 (Z0, A0, B0);
  Adder #(.width(1)) adder_1 (.a(and_7_out), .b(and_8_out), .out(Z1), .cout(adder_1_cout));  // open: cin
  Adder #(.width(1)) adder_2 (.a(and_5_out), .b(and_6_out), .out(adder_2_out), .cin(adder_1_cout), .cout(adder_2_cout));
  Adder #(.width(1)) adder_3 (.a(and_4_out), .b(adder_2_cout), .out(adder_3_out), .cout(adder_3_cout));  // open: cin
  Adder #(.width(1)) adder_4 (.a(and_3_out), .b(adder_2_out), .out(Z2), .cout(adder_4_cout));  // open: cin
  Adder #(.width(1)) adder_5 (.a(and_1_out), .b(adder_3_cout), .out(Z4), .cin(adder_6_cout), .cout(Z5));
  Adder #(.width(1)) adder_6 (.a(and_2_out), .b(adder_3_out), .out(Z3), .cin(adder_4_cout), .cout(adder_6_cout));

  // Notes on the sheet:
  //   (A2.B2)
  //   (A1.B2)
  //   (A0.B2)
  //   (A2.B1)
  //   (A1.B1)
  //   (A2.B0)
  //   (A0.B1)
  //   (A1.B0)
  //   (A0.B0)
  //   HALF ADDER
  //   HALF ADDER
  //   S4
  //   FULL ADDER
  //   3 BIT MULTIPLIER
  //   S3
  //   S2
  //   FULL ADDER
  //   FULL ADDER
  //   HALF ADDER
endmodule
