// Logisim project Magnitude comparator.circ as structural Verilog: 1 circuit, main circuit main
module main (
  input  [3:0] in_1,
  input  [3:0] in_2,
  output out_3,
  output out_4,
  output out_5
);

  wire and_1_out, and_2_out, and_3_out, and_4_out, and_5_out, and_6_out, and_7_out, and_8_out, not_1_out,
       not_2_out, not_3_out, not_4_out, not_5_out, not_6_out, not_7_out, not_8_out, xnor_1_out, xnor_2_out,
       xnor_3_out, xnor_4_out;

  xnor xnor_1 (xnor_1_out, in_1[0], in_2[0]);
  xnor xnor_2 (xnor_2_out, in_1[1], in_2[1]);
  xnor xnor_3 (xnor_3_out, in_1[2], in_2[2]);
  xnor xnor_4 (xnor_4_out, in_1[3], in_2[3]);
  not not_1 (not_1_out, in_2[3]);
  not not_2 (not_2_out, in_1[2]);
  and and_1 (and_1_out, not_1_out, in_1[3]);
  not not_3 (not_3_out, in_2[2]);
  and and_2 (and_2_out, xnor_4_out, xnor_3_out, in_1[1], not_4_out);
  not not_4 (not_4_out, in_2[1]);
  not not_5 (not_5_out, in_2[0]);
  not not_6 (not_6_out, in_1[0]);
  not not_7 (not_7_out, in_1[1]);
  and and_3 (and_3_out, xnor_4_out, not_2_out, in_2[2]);
  not not_8 (not_8_out, in_1[3]);
  and and_4 (and_4_out, xnor_4_out, in_1[2], not_3_out);
  and and_5 (and_5_out, xnor_3_out, xnor_4_out, in_1[0], not_5_out, xnor_2_out);
  and and_6 (and_6_out, xnor_4_out, xnor_3_out, xnor_2_out, in_2[0], not_6_out);
  and and_7 (and_7_out, xnor_4_out, xnor_3_out, in_2[1], not_7_out);
  and and_8 (and_8_out, not_8_out, in_2[3]);
  and and_9 (out_3, xnor_1_out, xnor_2_out, xnor_3_out, xnor_4_out);
  or or_1 (out_4, and_1_out, and_4_out, and_2_out, and_5_out);
  or or_2 (out_5, and_6_out, and_7_out, and_3_out, and_8_out);

  // Notes on the sheet:
  //   A0
  //   A1
  //   A2
  //   A3
  //   B0
  //   B1
  //   B2
  //   B3
  //   Rules to be followed:
  //   A0 XNOR B0
  //   A1 XNOR B1
  //   A2 XNOR B2
  //   A3 XNOR B3
  //   When one of it goes true, it won't check the next one.
  //   Thus initially checking for MSB and then the next bits onwards.
  //   4-BIT COMPARATOR
  //   1. Here, for First Case where both inputs are equal we have to check each an every bit
  //   Hence we have used XNOR Gate which gives o/p '1' when both bits are equal.
  //   DFH
  //   A3.B3'
  //   E3.E2.A1.B1'
  //   E3.A2'.B2
  //   2. Secondly, for 'A<B' we are going in ascending fashion where we are checking from the MSB to LSB 
  //   E3.A2.B2'
  //   E3.E2.E1.A0.B0'
  //   E3.E2.E1.A0'.B0
  //   E3.E2.A1'.B1
  //   A3'.B3
  //   3. Thirdly, for 'A<B'  we are going in ascending fashion same as above and similarly we have taken into consideration all possible outcomes
  //   A=B
  //   A>B
  //   A<B
endmodule
