// Logisim project p1.circ as structural Verilog: 3 circuits, main circuit main
module main (
  input  [5:0] in_1,
  input  [5:0] in_2,
  input  in_3,
  input  [5:0] in_4,
  input  in_5,
  input  in_6,
  input  [5:0] in_7,
  input  [5:0] in_8,
  output [5:0] out_9
);

  wire binary_to_decimal_1_a_2, binary_to_decimal_1_b_2, binary_to_decimal_1_c_2, binary_to_decimal_1_d_2,
       binary_to_decimal_1_e_2, binary_to_decimal_1_f_2, binary_to_decimal_1_g, clock_1_out, clock_2_out,
       n6_bit_equaliser_1_a_b, n6_bit_equaliser_2_a_b;
  wire [5:0] adder_1_out, bit_extender_1_out, counter_1_q, counter_2_q, divider_1_rem, divider_2_rem;

  Divider #(.width(6)) divider_1 (.a(in_4), .b(adder_1_out), .rem(divider_1_rem));  // open: out, upper
  Counter #(.width(6), .max('h3f), .ongoal("stay")) counter_1 (
    .load(in_5), .count(in_6), .Q(counter_1_q), .clk(clock_1_out));  // open: D, carry, clr
  Clock clock_1 (.out(clock_1_out));
  Divider #(.width(6)) divider_2 (.a(counter_1_q), .b(in_7), .rem(divider_2_rem));  // open: out, upper
  _6__BIT_Equaliser u_6_bit_equaliser_1 (.INPUT_A(in_1), .INPUT_B(divider_1_rem), .A_B(n6_bit_equaliser_1_a_b));
  _6__BIT_Equaliser u_6_bit_equaliser_2 (.INPUT_A(divider_2_rem), .INPUT_B(in_8), .A_B(n6_bit_equaliser_2_a_b));
  assign bit_extender_1_out = {{5{1'b0}}, n6_bit_equaliser_2_a_b};  // Bit_Extender bit_extender_1
  Adder #(.width(6)) adder_1 (.a(counter_1_q), .b(bit_extender_1_out), .out(adder_1_out));  // open: cin, cout
  Counter #(.width(6), .max('h3f), .ongoal("continue")) counter_2 (
    .load(in_3), .count(n6_bit_equaliser_1_a_b), .Q(counter_2_q), .clk(clock_2_out));  // open: D, carry, clr
  Clock clock_2 (.out(clock_2_out));
  Divider #(.width(6)) divider_3 (.a(counter_2_q), .b(in_2), .out(out_9));  // open: upper, rem
  Binary_to_Decimal binary_to_decimal_1 (
    .A(out_9[5]), .B(out_9[4]), .C(out_9[3]), .a_2(binary_to_decimal_1_a_2), .D(out_9[2]), .E(out_9[1]),
    .F(out_9[0]), .b_2(binary_to_decimal_1_b_2), .c_2(binary_to_decimal_1_c_2),
    .d_2(binary_to_decimal_1_d_2), .e_2(binary_to_decimal_1_e_2), .f_2(binary_to_decimal_1_f_2),
    .g(binary_to_decimal_1_g));
  _7_Segment_Display u_7_segment_display_1 (
    .g(binary_to_decimal_1_g), .f(binary_to_decimal_1_f_2), .a(binary_to_decimal_1_a_2),
    .b(binary_to_decimal_1_b_2), .e(binary_to_decimal_1_e_2), .d(binary_to_decimal_1_d_2),
    .c(binary_to_decimal_1_c_2));  // open: dp
endmodule

module Binary_to_Decimal (
  input  A,
  input  B,
  input  C,
  input  D,
  input  E,
  input  F,
  output a_2,
  output b_2,
  output c_2,
  output d_2,
  output e_2,
  output f_2,
  output g
);

  wire and_1_out, and_2_out, and_3_out, and_4_out, and_5_out, and_6_out, and_7_out, and_8_out, and_9_out,
       and_10_out, and_11_out, and_12_out, and_13_out, and_14_out, and_15_out, and_16_out, and_17_out,
       not_1_out, not_2_out, not_3_out, not_4_out, not_5_out, not_6_out, not_7_out, not_8_out, not_9_out,
       not_10_out, not_11_out, not_12_out, not_13_out, not_14_out, not_15_out, not_16_out, not_17_out,
       not_18_out, not_19_out, not_20_out, not_21_out, not_22_out, not_23_out, not_24_out, not_25_out;

  not not_1 (not_1_out, A);
  not not_2 (not_2_out, C);
  not not_3 (not_3_out, A);
  not not_4 (not_4_out, D);
  not not_5 (not_5_out, E);
  not not_6 (not_6_out, F);
  not not_7 (not_7_out, B);
  not not_8 (not_8_out, C);
  not not_9 (not_9_out, B);
  not not_10 (not_10_out, A);
  not not_11 (not_11_out, C);
  not not_12 (not_12_out, A);
  not not_13 (not_13_out, C);
  not not_14 (not_14_out, B);
  not not_15 (not_15_out, A);
  not not_16 (not_16_out, C);
  not not_17 (not_17_out, C);
  not not_18 (not_18_out, B);
  not not_19 (not_19_out, C);
  not not_20 (not_20_out, B);
  not not_21 (not_21_out, C);
  not not_22 (not_22_out, A);
  not not_23 (not_23_out, B);
  not not_24 (not_24_out, C);
  and and_1 (and_1_out, not_1_out, not_2_out);
  and and_2 (and_2_out, not_3_out, not_4_out, not_5_out, not_6_out);
  and and_3 (and_3_out, A, C);
  not not_25 (not_25_out, A);
  and and_4 (and_4_out, not_7_out, not_8_out);
  and and_5 (and_5_out, B, C);
  or or_1 (c_2, not_9_out, C, A);
  and and_6 (and_6_out, not_10_out, not_11_out);
  and and_7 (and_7_out, not_12_out, B);
  and and_8 (and_8_out, B, not_13_out);
  and and_9 (and_9_out, A, not_14_out, C);
  and and_10 (and_10_out, not_15_out, not_16_out);
  and and_11 (and_11_out, B, not_17_out);
  and and_12 (and_12_out, not_18_out, not_19_out);
  and and_13 (and_13_out, A, not_20_out);
  and and_14 (and_14_out, A, not_21_out);
  and and_15 (and_15_out, not_22_out, B);
  and and_16 (and_16_out, A, not_23_out);
  and and_17 (and_17_out, A, not_24_out);
  or or_2 (a_2, and_1_out, and_2_out, B, and_3_out);
  or or_3 (b_2, not_25_out, and_4_out, and_5_out);
  or or_4 (d_2, and_6_out, and_7_out, and_8_out, and_9_out);
  or or_5 (e_2, and_10_out, and_11_out);
  or or_6 (f_2, and_12_out, and_13_out, and_14_out);
  or or_7 (g, and_15_out, and_16_out, and_17_out);
endmodule

module _6__BIT_Equaliser (
  input  [5:0] INPUT_A,
  input  [5:0] INPUT_B,
  output A_B
);

  wire and_1_out, and_2_out, and_3_out, and_4_out, and_5_out, and_6_out, and_7_out, and_8_out, and_9_out,
       and_10_out, and_11_out, and_12_out, not_1_out, not_2_out, not_3_out, not_4_out, not_5_out, not_6_out,
       not_7_out, not_8_out, not_9_out, not_10_out, not_11_out, not_12_out, not_13_out, not_14_out,
       not_15_out, not_16_out, not_17_out, not_18_out, or_1_out, or_2_out, or_3_out, or_4_out, or_5_out,
       or_6_out;

  not not_1 (not_1_out, INPUT_A[5]);
  not not_2 (not_2_out, INPUT_B[5]);
  not not_3 (not_3_out, INPUT_A[4]);
  not not_4 (not_4_out, INPUT_B[4]);
  not not_5 (not_5_out, INPUT_A[3]);
  not not_6 (not_6_out, INPUT_B[3]);
  not not_7 (not_7_out, INPUT_A[2]);
  not not_8 (not_8_out, INPUT_B[2]);
  not not_9 (not_9_out, INPUT_A[1]);
  not not_10 (not_10_out, INPUT_B[1]);
  not not_11 (not_11_out, INPUT_A[0]);
  not not_12 (not_12_out, INPUT_B[0]);
  and and_1 (and_1_out, not_1_out, INPUT_B[5]);
  and and_2 (and_2_out, INPUT_A[5], not_2_out);
  and and_3 (and_3_out, not_3_out, INPUT_B[4]);
  and and_4 (and_4_out, INPUT_A[4], not_4_out);
  and and_5 (and_5_out, not_5_out, INPUT_B[3]);
  and and_6 (and_6_out, INPUT_A[3], not_6_out);
  and and_7 (and_7_out, not_7_out, INPUT_B[2]);
  and and_8 (and_8_out, INPUT_A[2], not_8_out);
  and and_9 (and_9_out, not_9_out, INPUT_B[1]);
  and and_10 (and_10_out, INPUT_A[1], not_10_out);
  and and_11 (and_11_out, not_11_out, INPUT_B[0]);
  and and_12 (and_12_out, INPUT_A[0], not_12_out);
  or or_1 (or_1_out, and_1_out, and_2_out);
  not not_13 (not_13_out, or_1_out);
  not not_14 (not_14_out, or_2_out);
  or or_2 (or_2_out, and_3_out, and_4_out);
  not not_15 (not_15_out, or_3_out);
  or or_3 (or_3_out, and_5_out, and_6_out);
  not not_16 (not_16_out, or_4_out);
  or or_4 (or_4_out, and_7_out, and_8_out);
  or or_5 (or_5_out, and_9_out, and_10_out);
  not not_17 (not_17_out, or_5_out);
  not not_18 (not_18_out, or_6_out);
  or or_6 (or_6_out, and_11_out, and_12_out);
  and and_13 (A_B, not_13_out, not_14_out, not_15_out, not_16_out, not_17_out, not_18_out);

  // Notes on the sheet:
  //   A5
  //   B5
  //   A4
  //   B4
  //   A3
  //   B3
  //   A2
  //   B2
  //   A1
  //   B1
  //   A0
  //   B0
  //   X5
  //   X4
  //   X3
  //   X2
  //   X1
  //   X0
endmodule
