// Logisim project polite.circ as structural Verilog: 3 circuits, main circuit main
module main (
  input  [5:0] _0,
  input  [5:0] INPUT,
  input  [5:0] _0_2,
  input  [5:0] _1,
  input  [5:0] _111111,
  input  [5:0] _2,
  input  [5:0] _2_2,
  input  [5:0] _0_3
);

  wire binary_to_decimal_1_a_2, binary_to_decimal_1_b_2, binary_to_decimal_1_c_2, binary_to_decimal_1_d_2,
       binary_to_decimal_1_e_2, binary_to_decimal_1_f_2, binary_to_decimal_1_g, CLOCK_2_out, CLOCK_out,
       multiplexer_1_out, n6_bit_equaliser_1_equal_value, n6_bit_equaliser_2_equal_value,
       n6_bit_equaliser_3_equal_value;
  wire [5:0] adder_1_out, adder_2_out, bit_extender_1_out, divider_1_rem, divider_2_rem, divider_3_out,
       multiplexer_2_out, START_WITH_0_q, START_WITH_2_q;

  Counter #(.width(6), .max('h3f), .ongoal("stay")) START_WITH_2 (
    .load(1'b0), .count(1'b1), .Q(START_WITH_2_q), .clk(CLOCK_out));  // open: D, carry, clr
  Clock CLOCK (.out(CLOCK_out));
  Divider #(.width(6)) divider_1 (.a(INPUT), .b(adder_1_out), .rem(divider_1_rem));  // open: out, upper
  _6___BIT_Equaliser u_6_bit_equaliser_1 (
    .INPUT_B(_0), .Equal_Value(n6_bit_equaliser_1_equal_value), .INPUT_A(divider_1_rem));
  _6___BIT_Equaliser u_6_bit_equaliser_2 (
    .INPUT_B(_111111), .Equal_Value(n6_bit_equaliser_2_equal_value), .INPUT_A(START_WITH_2_q));
  Divider #(.width(6)) divider_2 (.a(START_WITH_2_q), .b(_2_2), .rem(divider_2_rem));  // open: out, upper
  _6___BIT_Equaliser u_6_bit_equaliser_3 (
    .INPUT_B(divider_2_rem), .Equal_Value(n6_bit_equaliser_3_equal_value), .INPUT_A(_0_3));
  Multiplexer multiplexer_1 (
    .in0(n6_bit_equaliser_1_equal_value), .in1(1'b0), .out(multiplexer_1_out),
    .sel(n6_bit_equaliser_2_equal_value));  // open: en
  assign bit_extender_1_out = {{5{1'b0}}, n6_bit_equaliser_3_equal_value};  // Bit_Extender bit_extender_1
  Adder #(.width(6)) adder_1 (.a(START_WITH_2_q), .b(bit_extender_1_out), .out(adder_1_out));  // open: cin, cout
  Counter #(.width(6), .max('h3f), .ongoal("continue")) START_WITH_0 (
    .load(1'b0), .count(multiplexer_1_out), .Q(START_WITH_0_q), .clk(CLOCK_2_out));  // open: D, carry, clr
  Clock CLOCK_2 (.out(CLOCK_2_out));
  Multiplexer #(.width(6)) multiplexer_2 (
    .in0(_0_2), .in1(_1), .out(multiplexer_2_out), .sel(n6_bit_equaliser_2_equal_value));  // open: en
  Adder #(.width(6)) adder_2 (.a(multiplexer_2_out), .b(START_WITH_0_q), .out(adder_2_out));  // open: cin, cout
  Divider #(.width(6)) divider_3 (.a(adder_2_out), .b(_2), .out(divider_3_out));  // open: upper, rem
  Binary_to_Decimal binary_to_decimal_1 (
    .A(divider_3_out[5]), .B(divider_3_out[4]), .C(divider_3_out[3]), .D(divider_3_out[2]),
    .E(divider_3_out[1]), .a_2(binary_to_decimal_1_a_2), .F(divider_3_out[0]), .b_2(binary_to_decimal_1_b_2),
    .c_2(binary_to_decimal_1_c_2), .d_2(binary_to_decimal_1_d_2), .e_2(binary_to_decimal_1_e_2),
    .f_2(binary_to_decimal_1_f_2), .g(binary_to_decimal_1_g));
  _7_Segment_Display u_7_segment_display_1 (
    .g(binary_to_decimal_1_g), .f(binary_to_decimal_1_f_2), .a(binary_to_decimal_1_a_2),
    .b(binary_to_decimal_1_b_2), .e(binary_to_decimal_1_e_2), .d(binary_to_decimal_1_d_2),
    .c(binary_to_decimal_1_c_2));  // open: dp

  // Notes on the sheet:
  //   Main Logic:
  //   TO CHECK FOR EVEN NO.
  //   INPUT: Maximum 6- Bit.
  //   change it to next odd number.
  //   SHIFS TO 1 AND STOPS THE COUNTER
  //   SPECIFIC FOR 63
  //   EXTENDS 1->6
  //   For eg. the i/p is 15 the o/p must be 3.
  //   For eg. when the number arrives 2, we turn it to 3.
  //   But here MUX are specifically used to handle i/p 63.
  //   POLITENESS OF NUMBER
  //   ADDS THE O/P TO ORIGINAL I/P
  //   Hence for 15 it is 1,3,5,15 while excluding 1, total number is 3.
  //   2. Thus the trick here is whenever an even number arries we outwardly
  //   Hence to stop that counterat that specific i/p  MUX are used.
  //   3. Similarly at the end by using a divider we change it to the original count
  //   As when both load and count are '0' it leads counter to 'stop' state.
  //   1. To find the poltiness we need to calculate the odd divisor which is greater than 1.
  //   4. Using an extender, we change 1 bit o/p of equaliser to 6 bit to carryon the flow.
  //   5. Then by finally finding the divisor, and using equaliser the required o/p arrives.
  //   ADDS THE DIFF. FOR 63
  //   FINAL DIVIDING 
  //   As the maximum limit of 6- Bit counter is 63, and as it divides by itself the 2nd counter continues to increase.
  //   POLITENESS
endmodule

// Bin to Dec
module Binary_to_Decimal (
  input  A,
  input  B,
  input  C,
  input  D,
  input  E,
  input  F,
  output a_2,
  output b_2,
  output c_2,
  output d_2,
  output e_2,
  output f_2,
  output g
);

  wire and_1_out, and_2_out, and_3_out, and_4_out, and_5_out, and_6_out, and_7_out, and_8_out, and_9_out,
       and_10_out, and_11_out, and_12_out, and_13_out, and_14_out, and_15_out, and_16_out, and_17_out,
       and_18_out, and_19_out, and_20_out, and_21_out, and_22_out, and_23_out, and_24_out, and_25_out,
       and_26_out, and_27_out, and_28_out, and_29_out, and_30_out, and_31_out, and_32_out, and_33_out,
       and_34_out, and_35_out, not_1_out, not_2_out, not_3_out, not_4_out, not_5_out, not_6_out, not_7_out,
       not_8_out, not_9_out, not_10_out, not_11_out, not_12_out, not_13_out, not_14_out, not_15_out,
       not_16_out, not_17_out, not_18_out, not_19_out, not_20_out, not_21_out, not_22_out, not_23_out,
       not_24_out, not_25_out, not_26_out, not_27_out, not_28_out, not_29_out, not_30_out, not_31_out,
       not_32_out, not_33_out, not_34_out, not_35_out, not_36_out, not_37_out, not_38_out, not_39_out,
       not_40_out, not_41_out, not_42_out, not_43_out, not_44_out, not_45_out, not_46_out, not_47_out,
       not_48_out, not_49_out, not_50_out, not_51_out, not_52_out, not_53_out, not_54_out, not_55_out,
       not_56_out, not_57_out, not_58_out, not_59_out, not_60_out, not_61_out, not_62_out, not_63_out,
       not_64_out, not_65_out, not_66_out, not_67_out;

  not not_1 (not_1_out, A);
  not not_2 (not_2_out, D);
  not not_3 (not_3_out, E);
  not not_4 (not_4_out, F);
  not not_5 (not_5_out, A);
  not not_6 (not_6_out, C);
  not not_7 (not_7_out, A);
  not not_8 (not_8_out, C);
  not not_9 (not_9_out, A);
  not not_10 (not_10_out, D);
  not not_11 (not_11_out, A);
  not not_12 (not_12_out, E);
  not not_13 (not_13_out, F);
  not not_14 (not_14_out, A);
  not not_15 (not_15_out, A);
  not not_16 (not_16_out, A);
  not not_17 (not_17_out, B);
  not not_18 (not_18_out, C);
  not not_19 (not_19_out, B);
  not not_20 (not_20_out, E);
  not not_21 (not_21_out, B);
  not not_22 (not_22_out, B);
  not not_23 (not_23_out, A);
  not not_24 (not_24_out, C);
  not not_25 (not_25_out, D);
  not not_26 (not_26_out, F);
  not not_27 (not_27_out, A);
  not not_28 (not_28_out, C);
  not not_29 (not_29_out, D);
  not not_30 (not_30_out, A);
  not not_31 (not_31_out, C);
  not not_32 (not_32_out, F);
  not not_33 (not_33_out, A);
  not not_34 (not_34_out, C);
  not not_35 (not_35_out, E);
  not not_36 (not_36_out, A);
  not not_37 (not_37_out, C);
  not not_38 (not_38_out, B);
  not not_39 (not_39_out, A);
  not not_40 (not_40_out, C);
  not not_41 (not_41_out, D);
  not not_42 (not_42_out, F);
  not not_43 (not_43_out, A);
  not not_44 (not_44_out, C);
  not not_45 (not_45_out, F);
  not not_46 (not_46_out, C);
  not not_47 (not_47_out, B);
  not not_48 (not_48_out, C);
  not not_49 (not_49_out, E);
  not not_50 (not_50_out, F);
  not not_51 (not_51_out, B);
  not not_52 (not_52_out, C);
  not not_53 (not_53_out, E);
  not not_54 (not_54_out, B);
  not not_55 (not_55_out, C);
  not not_56 (not_56_out, F);
  not not_57 (not_57_out, B);
  not not_58 (not_58_out, C);
  not not_59 (not_59_out, C);
  not not_60 (not_60_out, D);
  not not_61 (not_61_out, C);
  not not_62 (not_62_out, E);
  not not_63 (not_63_out, C);
  not not_64 (not_64_out, F);
  not not_65 (not_65_out, A);
  not not_66 (not_66_out, B);
  not not_67 (not_67_out, C);
  and and_1 (and_1_out, not_1_out, not_2_out, not_3_out, not_4_out);
  and and_2 (and_2_out, not_5_out, not_6_out, E);
  and and_3 (and_3_out, not_7_out, not_8_out, D, F);
  and and_4 (and_4_out, A, C);
  and and_5 (and_5_out, not_9_out, not_10_out);
  and and_6 (and_6_out, not_11_out, not_12_out, not_13_out);
  and and_7 (and_7_out, not_14_out, E, F);
  and and_8 (and_8_out, not_15_out, C);
  and and_9 (and_9_out, not_16_out, B);
  and and_10 (and_10_out, B, C);
  and and_11 (and_11_out, A, not_17_out, not_18_out);
  and and_12 (and_12_out, not_19_out, not_20_out);
  and and_13 (and_13_out, not_21_out, F);
  and and_14 (and_14_out, not_22_out, D);
  and and_15 (and_15_out, not_23_out, not_24_out, not_25_out, not_26_out);
  and and_16 (and_16_out, not_27_out, not_28_out, not_29_out, E);
  and and_17 (and_17_out, not_30_out, not_31_out, E, not_32_out);
  and and_18 (and_18_out, not_33_out, not_34_out, D, not_35_out, F);
  and and_19 (and_19_out, not_36_out, B);
  and and_20 (and_20_out, B, not_37_out);
  and and_21 (and_21_out, A, not_38_out, C);
  and and_22 (and_22_out, not_39_out, not_40_out, not_41_out, not_42_out);
  and and_23 (and_23_out, not_43_out, not_44_out, E, not_45_out);
  and and_24 (and_24_out, B, not_46_out);
  and and_25 (and_25_out, not_47_out, not_48_out, not_49_out, not_50_out);
  and and_26 (and_26_out, not_51_out, not_52_out, D, not_53_out);
  and and_27 (and_27_out, not_54_out, not_55_out, D, not_56_out);
  and and_28 (and_28_out, A, not_57_out);
  and and_29 (and_29_out, A, not_58_out);
  and and_30 (and_30_out, not_59_out, not_60_out, E);
  and and_31 (and_31_out, not_61_out, D, not_62_out);
  and and_32 (and_32_out, not_63_out, D, not_64_out);
  and and_33 (and_33_out, not_65_out, B);
  and and_34 (and_34_out, A, not_66_out);
  and and_35 (and_35_out, A, not_67_out);
  or or_1 (a_2, and_1_out, and_2_out, and_3_out, B, and_4_out);
  or or_2 (b_2, and_5_out, and_6_out, and_7_out, and_8_out, and_9_out, and_10_out, and_11_out);
  or or_3 (c_2, and_12_out, and_13_out, and_14_out, C, A);
  or or_4 (d_2, and_15_out, and_16_out, and_17_out, and_18_out, and_19_out, and_20_out, and_21_out);
  or or_5 (e_2, and_22_out, and_23_out, and_24_out);
  or or_6 (f_2, and_25_out, and_26_out, and_27_out, and_28_out, and_29_out);
  or or_7 (g, and_30_out, and_31_out, and_32_out, and_33_out, and_34_out, and_35_out);

  // Notes on the sheet:
  //   Steps followed:
  //   2. I followed the default naming convention.
  //   f
  //   e
  //   3. Here basic gates are used for implementation.
  //   a
  //   b
  //   g
  //   c
  //   d
  //   4. While the wires are attached acc. to the convention.
  //   BINARY TO DECIMAL
  //   1. Here using the logic of 7 Segment Display Logic,i made a circuit.
endmodule

// Equaliser
module _6___BIT_Equaliser (
  input  [5:0] INPUT_A,
  input  [5:0] INPUT_B,
  output Equal_Value
);

  wire and_1_out, and_2_out, and_3_out, and_4_out, and_5_out, and_6_out, and_7_out, and_8_out, and_9_out,
       and_10_out, and_11_out, and_12_out, not_1_out, not_2_out, not_3_out, not_4_out, not_5_out, not_6_out,
       not_7_out, not_8_out, not_9_out, not_10_out, not_11_out, not_12_out, not_13_out, not_14_out,
       not_15_out, not_16_out, not_17_out, not_18_out, or_1_out, or_2_out, or_3_out, or_4_out, or_5_out,
       or_6_out;

  not not_1 (not_1_out, INPUT_A[5]);
  not not_2 (not_2_out, INPUT_B[5]);
  not not_3 (not_3_out, INPUT_A[4]);
  not not_4 (not_4_out, INPUT_B[4]);
  not not_5 (not_5_out, INPUT_A[3]);
  not not_6 (not_6_out, INPUT_B[3]);
  not not_7 (not_7_out, INPUT_A[2]);
  not not_8 (not_8_out, INPUT_B[2]);
  not not_9 (not_9_out, INPUT_A[1]);
  not not_10 (not_10_out, INPUT_B[1]);
  not not_11 (not_11_out, INPUT_A[0]);
  not not_12 (not_12_out, INPUT_B[0]);
  and and_1 (and_1_out, not_1_out, INPUT_B[5]);
  and and_2 (and_2_out, INPUT_A[5], not_2_out);
  and and_3 (and_3_out, not_3_out, INPUT_B[4]);
  and and_4 (and_4_out, INPUT_A[4], not_4_out);
  and and_5 (and_5_out, not_5_out, INPUT_B[3]);
  and and_6 (and_6_out, INPUT_A[3], not_6_out);
  and and_7 (and_7_out, not_7_out, INPUT_B[2]);
  and and_8 (and_8_out, INPUT_A[2], not_8_out);
  and and_9 (and_9_out, not_9_out, INPUT_B[1]);
  and and_10 (and_10_out, INPUT_A[1], not_10_out);
  and and_11 (and_11_out, not_11_out, INPUT_B[0]);
  and and_12 (and_12_out, INPUT_A[0], not_12_out);
  or or_1 (or_1_out, and_1_out, and_2_out);
  not not_13 (not_13_out, or_1_out);
  not not_14 (not_14_out, or_2_out);
  or or_2 (or_2_out, and_3_out, and_4_out);
  not not_15 (not_15_out, or_3_out);
  or or_3 (or_3_out, and_5_out, and_6_out);
  not not_16 (not_16_out, or_4_out);
  or or_4 (or_4_out, and_7_out, and_8_out);
  or or_5 (or_5_out, and_9_out, and_10_out);
  not not_17 (not_17_out, or_5_out);
  or or_6 (or_6_out, and_11_out, and_12_out);
  not not_18 (not_18_out, or_6_out);
  and and_13 (Equal_Value, not_13_out, not_14_out, not_15_out, not_16_out, not_17_out, not_18_out);

  // Notes on the sheet:
  //   Step followed:
  //   or lesser was not useful in the circuit.
  //   1. Here using the logic of comparator, i made the circuit.
  //   2. While the number showing comparision in terms of greater 
  //   A5
  //   B5
  //   A4
  //   B4
  //   A3
  //   B3
  //   A2
  //   B2
  //   A1
  //   B1
  //   A0
  //   B0
  //   4. Using basic logic gates i.e AND, OR and NOT it was implemented.
  //   6 - BIT EQUALISER 
  //   3. Thus using XNOR Gates which is even called Equivalence Gate the circuit was made. 
  //   X5 = A5'B5' + A5B5
  //   X4 = A4'B4' + A4B4
  //   X3 = A3'B3' + A3B3
  //   X2 = A2'B2' + A2B2
  //   X1 = A1'B1' + A1B1
  //   X0 = A0'B0' + A0B0
  //   Z= X0.X1.X2.X3.X4.X5
  //   A=B
endmodule
